// Logisim project projeto.circ as structural Verilog: 4 circuits, main circuit main
module main (
  input  in_1
);

  wire CLK;
  wire [31:0] instructionf_1_instrucao;

  Clock clock_1 (.out(CLK));
  // Probe on instructionf_1_instrucao
  InstructionF instructionf_1 (.CLK(CLK), .RST(in_1), .Instrucao(instructionf_1_instrucao));
  IntructionD intructiond_1 (.Instrucao(instructionf_1_instrucao));  // open: opcode, rd, funct3, rs1, rs2, funct7, I_Imm, S_Imm, B_Imm, U_Imm, J_Imm

  // Other names for the same wires on the sheet: RST = in_1
endmodule

module InstructionF (
  input  CLK,
  input  RST,
  output [31:0] Instrucao
);

  wire [7:0] adder_1_out, PC_q;

  Register PC (.D(adder_1_out), .en(1'b1), .clk(CLK), .Q(PC_q), .clr(RST));
  // Probe on adder_1_out
  // ROM #(.line("quad")) rom_1: pin names not known; wires that end beside it: PC_q
  Adder adder_1 (.a(8'h4), .b(PC_q), .out(adder_1_out));  // open: cin, cout

  // Notes on the sheet:
  //   contents of rom_1 (hex, n*v repeats v):
  //   93 0 50 0 13 1 70 0 93 2 0 0 b3 8 20 0 33 2 11 40 23 a0 32 0 23 a2 42 0 33 f 2 0 b3 e 2 0 63 86 10 0
  //   93 1 30 6 13 3 10 0 3 a4 2 0 83 a4 42 0 6f 5 80 0 93 1 30 6 93 5 10
  //   Memoria de instrucoes
endmodule

module IntructionD (
  input  [31:0] Instrucao,
  output [6:0] opcode,
  output [4:0] rd,
  output [2:0] funct3,
  output [4:0] rs1,
  output [4:0] rs2,
  output [6:0] funct7,
  output [11:0] I_Imm,
  output [11:0] S_Imm,
  output [11:0] B_Imm,
  output [19:0] U_Imm,
  output [19:0] J_Imm
);


  assign B_Imm = {Instrucao[25], Instrucao[7], Instrucao[31:26], Instrucao[11:8]};
  assign funct3 = Instrucao[14:12];
  assign funct7 = Instrucao[31:25];
  assign I_Imm = Instrucao[31:20];
  assign J_Imm = {Instrucao[31], Instrucao[21:12], Instrucao[22], Instrucao[30:23]};
  assign opcode = Instrucao[6:0];
  assign rd = Instrucao[11:7];
  assign rs1 = Instrucao[19:15];
  assign rs2 = Instrucao[24:20];
  assign S_Imm = {Instrucao[31:25], Instrucao[11:7]};
  assign U_Imm = Instrucao[31:12];

  // Other names for the same wires on the sheet: b4_1[3:0] = Instrucao[11:8]; b10_5[5:0] = Instrucao[31:26];
  //   b19_12[7:0] = Instrucao[30:23]; b20 = Instrucao[31]; b11 = Instrucao[7]; b12 = Instrucao[25];
  //   b10_1[9:0] = Instrucao[21:12]; b11_J = Instrucao[22]

  // Notes on the sheet:
  //   Imediato Tipo U
  //   Imediato Tipo J
  //   Imediato Tipo I
  //   Imediato Tipo S
  //   Imediato Tipo B
endmodule

module BR (
  input  CLK,
  input  RST,
  input  RegWrite,
  input  [4:0] RS1,
  input  [4:0] RS2,
  input  [4:0] RD,
  input  [31:0] Data
);

  wire WE_X1, WE_X2, WE_X3, WE_X4, WE_X5, WE_X6, WE_X7, WE_X8, WE_X9, WE_X10, WE_X11, WE_X12, WE_X13, WE_X14,
       WE_X15, WE_X16, WE_X17, WE_X18, WE_X19, WE_X20, WE_X21, WE_X22, WE_X23, WE_X24, WE_X25, WE_X26,
       WE_X27, WE_X28, WE_X29, WE_X30, WE_X31;
  wire [31:0] Q_X, Q_X1, Q_X2, Q_X3, Q_X4, Q_X5, Q_X6, Q_X7, Q_X8, Q_X9, Q_X10, Q_X11, Q_X12, Q_X13, Q_X14,
       Q_X15, Q_X16, Q_X17, Q_X18, Q_X19, Q_X20, Q_X21, Q_X22, Q_X23, Q_X24, Q_X25, Q_X26, Q_X27, Q_X28,
       Q_X29, Q_X30, Q_X31;

  Demultiplexer #(.select(5)) demultiplexer_1 (
    .out1(WE_X1), .out2(WE_X2), .out3(WE_X3), .out4(WE_X4), .out5(WE_X5), .out6(WE_X6), .out7(WE_X7),
    .out8(WE_X8), .out9(WE_X9), .out10(WE_X10), .out11(WE_X11), .out12(WE_X12), .out13(WE_X13),
    .out14(WE_X14), .out15(WE_X15), .out16(WE_X16), .out17(WE_X17), .out18(WE_X18), .out19(WE_X19),
    .out20(WE_X20), .out21(WE_X21), .out22(WE_X22), .out23(WE_X23), .out24(WE_X24), .out25(WE_X25),
    .out26(WE_X26), .out27(WE_X27), .out28(WE_X28), .out29(WE_X29), .out30(WE_X30), .out31(WE_X31),
    .in(RegWrite), .sel(RD));  // open: out0
  Register #(.width(32)) x0 (.D({32{1'b0}}), .clk(CLK), .Q(Q_X), .clr(RST));  // open: en
  Register #(.width(32)) x4 (.D({32{1'b0}}), .en(WE_X4), .clk(CLK), .Q(Q_X4), .clr(RST));
  Register #(.width(32)) x8 (.D({32{1'b0}}), .en(WE_X8), .clk(CLK), .Q(Q_X8), .clr(RST));
  Register #(.width(32)) x12 (.D({32{1'b0}}), .en(WE_X12), .clk(CLK), .Q(Q_X12), .clr(RST));
  Register #(.width(32)) x16 (.D({32{1'b0}}), .en(WE_X16), .clk(CLK), .Q(Q_X16), .clr(RST));
  Register #(.width(32)) x20 (.D({32{1'b0}}), .en(WE_X20), .clk(CLK), .Q(Q_X20), .clr(RST));
  Register #(.width(32)) x24 (.D({32{1'b0}}), .en(WE_X24), .clk(CLK), .Q(Q_X24), .clr(RST));
  Register #(.width(32)) x28 (.D({32{1'b0}}), .en(WE_X28), .clk(CLK), .Q(Q_X28), .clr(RST));
  Register #(.width(32)) x1 (.D(Data), .en(WE_X1), .clk(CLK), .Q(Q_X1), .clr(RST));
  Register #(.width(32)) x5 (.D(Data), .en(WE_X5), .clk(CLK), .Q(Q_X5), .clr(RST));
  Register #(.width(32)) x9 (.D(Data), .en(WE_X9), .clk(CLK), .Q(Q_X9), .clr(RST));
  Register #(.width(32)) x13 (.D(Data), .en(WE_X13), .clk(CLK), .Q(Q_X13), .clr(RST));
  Register #(.width(32)) x17 (.D(Data), .en(WE_X17), .clk(CLK), .Q(Q_X17), .clr(RST));
  Register #(.width(32)) x21 (.D(Data), .en(WE_X21), .clk(CLK), .Q(Q_X21), .clr(RST));
  Register #(.width(32)) x25 (.D(Data), .en(WE_X25), .clk(CLK), .Q(Q_X25), .clr(RST));
  Register #(.width(32)) x29 (.D(Data), .en(WE_X29), .clk(CLK), .Q(Q_X29), .clr(RST));
  Register #(.width(32)) x2 (.D(Data), .en(WE_X2), .clk(CLK), .Q(Q_X2), .clr(RST));
  Register #(.width(32)) x6 (.D(Data), .en(WE_X6), .clk(CLK), .Q(Q_X6), .clr(RST));
  Register #(.width(32)) x10 (.D(Data), .en(WE_X10), .clk(CLK), .Q(Q_X10), .clr(RST));
  Register #(.width(32)) x14 (.D(Data), .en(WE_X14), .clk(CLK), .Q(Q_X14), .clr(RST));
  Register #(.width(32)) x18 (.D(Data), .en(WE_X18), .clk(CLK), .Q(Q_X18), .clr(RST));
  Register #(.width(32)) x22 (.D(Data), .en(WE_X22), .clk(CLK), .Q(Q_X22), .clr(RST));
  Register #(.width(32)) x26 (.D(Data), .en(WE_X26), .clk(CLK), .Q(Q_X26), .clr(RST));
  Register #(.width(32)) x30 (.D(Data), .en(WE_X30), .clk(CLK), .Q(Q_X30), .clr(RST));
  Register #(.width(32)) x3 (.D(Data), .en(WE_X3), .clk(CLK), .Q(Q_X3), .clr(RST));
  Register #(.width(32)) x7 (.D(Data), .en(WE_X7), .clk(CLK), .Q(Q_X7), .clr(RST));
  Register #(.width(32)) x11 (.D(Data), .en(WE_X11), .clk(CLK), .Q(Q_X11), .clr(RST));
  Register #(.width(32)) x15 (.D(Data), .en(WE_X15), .clk(CLK), .Q(Q_X15), .clr(RST));
  Register #(.width(32)) x19 (.D(Data), .en(WE_X19), .clk(CLK), .Q(Q_X19), .clr(RST));
  Register #(.width(32)) x23 (.D(Data), .en(WE_X23), .clk(CLK), .Q(Q_X23), .clr(RST));
  Register #(.width(32)) x27 (.D(Data), .en(WE_X27), .clk(CLK), .Q(Q_X27), .clr(RST));
  Register #(.width(32)) x31 (.D(Data), .en(WE_X31), .clk(CLK), .Q(Q_X31), .clr(RST));

  // Other names for the same wires on the sheet: RW = RegWrite
endmodule
