// Logisim project projetopentregar.circ as structural Verilog: 9 circuits, main circuit main
module main (
  input  RST
);

  wire ALUSrc, ALUZero, and_1_out, Branch, CLK, Jump, MemRead, MemToRead, MemWrite, RegWrite;
  wire [2:0] ALUOp, funct, OffSel, rd, rs1, rs2;
  wire [3:0] opcode;
  wire [5:0] B_offset, I_imm, S_offset;
  wire [8:0] J_offset;
  wire [15:0] ALU_Data, BRData, data, instrucao, NextPC, Offset_Imm, OffsetSel, OutDM, PC, PC2, PC_Branch,
       rd1, rd2, shifter_1_out, undriven;

  Clock u_CLK (.out(CLK));
  Multiplexer #(.width(16)) multiplexer_1 (.in0(Offset_Imm), .in1(rd2), .out(ALU_Data));  // open: sel
  IntructionF intructionf_1 (.CLK(CLK), .RST(RST), .NextPC(NextPC), .CurrentPC(PC), .Instrucao(instrucao));
  // Probe on instrucao
  Multiplexer #(.width(16)) multiplexer_2 (.in0(data), .in1(undriven), .out(BRData), .sel(MemToRead));
  InstuctionD instuctiond_1 (
    .Instrucao(instrucao), .funct(funct), .rs2(rs2), .rs1(rs1), .rd(rd), .opcode(opcode), .I_imm(I_imm),
    .S_offset(S_offset), .B_offset(B_offset), .J_offset(J_offset));
  UC uc_1 (
    .opcode(opcode), .funct(funct), .CLK(CLK), .RegWrite(RegWrite), .ALUSrc(ALUSrc), .Branch(Branch),
    .MemWrite(MemWrite), .Jump(Jump), .MemRead(MemRead), .MemToRead(MemToRead), .ALUOp(ALUOp), .OffSel(OffSel));
  // Probe on rd1
  BR br_1 (
    .CLK(CLK), .RST(RST), .RegWrite(RegWrite), .RS1(rs1), .RS2(rs2), .RD(rd), .Data(BRData), .rd1(rd1),
    .rd2(rd2));
  // Probe on rd2
  // Probe on OffsetSel
  ImmGen immgen_1 (
    .OffSel(OffSel), .I_Imm(I_imm), .S_Offset(S_offset), .B_Offset(B_offset), .J_Offset(J_offset),
    .Offset_Imm(OffsetSel));
  // Probe on OffsetSel
  Adder #(.width(16)) adder_1 (.a(16'h2), .b(PC), .out(PC2));  // open: cin, cout
  // Probe on rd1
  // Probe on PC2
  Shifter #(.width(16)) shifter_1 (.in(OffsetSel), .\dist (4'b0001), .out(shifter_1_out));
  // Probe on shifter_1_out
  // Probe on PC_Branch
  Adder #(.width(16)) adder_2 (.a(PC2), .b(shifter_1_out), .out(PC_Branch));  // open: cin, cout
  // Probe on NextPC
  Multiplexer #(.width(16)) multiplexer_3 (.in0(PC2), .in1(PC_Branch), .out(NextPC), .sel(and_1_out));
  and and_1 (and_1_out, Branch, ALUZero);
  ULA ula_1 (.src1(rd1), .src2(ALU_Data), .ALUOperation(ALUOp), .Result(data), .ALUZero(ALUZero));
  // Probe on OutDM
  DM dm_1 (.Address(data), .WriteEnable(MemWrite), .MemRead(MemRead), .CLK(CLK), .WriteData(rd2), .OutDM(OutDM));

  // Notes on the sheet:
  //   2° Entrada da ULA
  //   WriteBack BR
endmodule

module IntructionF (
  input  CLK,
  input  RST,
  input  [15:0] NextPC,
  output [15:0] CurrentPC,
  output [15:0] Instrucao
);

  Register #(.width(16)) PC (.D(NextPC), .en(1'b1), .clk(CLK), .Q(CurrentPC), .clr(RST));
  // ROM #(.addrWidth(10), .line("dual")) rom_1: pin names not known

  // Notes on the sheet:
  //   Memoria de instrucoes
endmodule

module InstuctionD (
  input  [15:0] Instrucao,
  output [2:0] funct,
  output [2:0] rs2,
  output [2:0] rs1,
  output [2:0] rd,
  output [3:0] opcode,
  output [5:0] I_imm,
  output [5:0] S_offset,
  output [5:0] B_offset,
  output [8:0] J_offset
);


  assign B_offset = Instrucao[5:0];
  assign funct = Instrucao[2:0];
  assign I_imm = Instrucao[5:0];
  assign J_offset = Instrucao[8:0];
  assign opcode = Instrucao[15:12];
  assign rd = Instrucao[11:9];
  assign rs1 = Instrucao[8:6];
  assign rs2 = Instrucao[5:3];
  assign S_offset = Instrucao[5:0];

  // Notes on the sheet:
  //   Imetiato Tipo I
  //   Offset Tipo B
  //   Offset Tipo S
  //   Offset Tipo J
endmodule

module BR (
  input  CLK,
  input  RST,
  input  RegWrite,
  input  [2:0] RS1,
  input  [2:0] RS2,
  input  [2:0] RD,
  input  [15:0] Data,
  output [15:0] rd1,
  output [15:0] rd2
);

  wire WE_R1, WE_R2, WE_R3, WE_R4, WE_R5, WE_R6, WE_R7;
  wire [15:0] Q_R0, Q_R1, Q_R2, Q_R3, Q_R4, Q_R5, Q_R6, Q_R7;

  Demultiplexer #(.select(3)) demultiplexer_1 (
    .out1(WE_R1), .out2(WE_R2), .out3(WE_R3), .out4(WE_R4), .out5(WE_R5), .out6(WE_R6), .out7(WE_R7),
    .in(RegWrite), .sel(RD));  // open: out0
  Register #(.trigger("falling"), .width(16)) R0 (.D({16{1'b0}}), .clk(CLK), .Q(Q_R0), .clr(RST));  // open: en
  Register #(.trigger("falling"), .width(16)) R4 (.D(Data), .en(WE_R4), .clk(CLK), .Q(Q_R4), .clr(RST));
  Register #(.width(16)) R1 (.D(Data), .en(WE_R1), .clk(CLK), .Q(Q_R1), .clr(RST));
  Register #(.trigger("falling"), .width(16)) R5 (.D(Data), .en(WE_R5), .clk(CLK), .Q(Q_R5), .clr(RST));
  Register #(.trigger("falling"), .width(16)) R2 (.D(Data), .en(WE_R2), .clk(CLK), .Q(Q_R2), .clr(RST));
  Register #(.trigger("falling"), .width(16)) R6 (.D(Data), .en(WE_R6), .clk(CLK), .Q(Q_R6), .clr(RST));
  Register #(.trigger("falling"), .width(16)) R3 (.D(Data), .en(WE_R3), .clk(CLK), .Q(Q_R3), .clr(RST));
  Register #(.trigger("falling"), .width(16)) R7 (.D(Data), .en(WE_R7), .clk(CLK), .Q(Q_R7), .clr(RST));
  Multiplexer #(.select(3), .width(16)) multiplexer_1 (
    .in0(Q_R0), .in1(Q_R1), .in2(Q_R2), .in3(Q_R3), .in4(Q_R4), .in5(Q_R5), .in6(Q_R6), .in7(Q_R7),
    .out(rd1), .sel(RS1));
  Multiplexer #(.select(3), .width(16)) multiplexer_2 (
    .in0(Q_R0), .in1(Q_R1), .in2(Q_R2), .in3(Q_R3), .in4(Q_R4), .in5(Q_R5), .in6(Q_R6), .in7(Q_R7),
    .out(rd2), .sel(RS2));

  // Other names for the same wires on the sheet: RW = RegWrite
endmodule

module ULA (
  input  [15:0] src1,
  input  [15:0] src2,
  input  [2:0] ALUOperation,
  output [15:0] Result,
  output ALUZero
);

  wire comparator_1_lt;
  wire [15:0] Add, And_Logic, Or_Logic, Slt_Logic, Sub;

  Adder #(.width(16)) adder_1 (.a(src1), .b(src2), .out(Add));  // open: cin, cout
  Subtractor #(.width(16)) subtractor_1 (.a(src1), .b(src2), .out(Sub));  // open: bin, bout
  assign And_Logic = src1 & src2;  // AND_Gate and_1, 16 bits wide
  assign Or_Logic = src1 | src2;  // OR_Gate or_1, 16 bits wide
  Comparator #(.width(16)) comparator_1 (.a(src1), .b(src2), .lt(comparator_1_lt));  // open: gt, eq
  assign Slt_Logic = {{15{1'b0}}, comparator_1_lt};  // Bit_Extender bit_extender_1
  // Probe on Result
  Multiplexer #(.select(3), .width(16)) multiplexer_1 (
    .in0(Add), .in1(Sub), .in2(And_Logic), .in3(Or_Logic), .in4(Slt_Logic), .out(Result), .sel(ALUOperation));  // open: in5, in6, in7
  // Probe on ALUZero
  Comparator #(.width(16)) comparator_2 (.a(Result), .b({16{1'b0}}), .eq(ALUZero));  // open: gt, lt

  // Other names for the same wires on the sheet: ALUOp[2:0] = ALUOperation

  // Notes on the sheet:
  //   Add
  //   Sub
  //   And
  //   Or
  //   Set Last Than
  //   ALUOp
  //   000 - Add (0)
  //   001 - Sub (1)
  //   010 - And (2)
  //   011 - Or (3)
  //   100 - Slt (4)
endmodule

module ImmGen (
  input  [2:0] OffSel,
  input  [5:0] I_Imm,
  input  [5:0] S_Offset,
  input  [5:0] B_Offset,
  input  [8:0] J_Offset,
  output [15:0] Offset_Imm
);

  wire [15:0] B_Offset16, Imm_16, J_Offset16, S_Offset16;

  assign B_Offset16 = {{9{B_Offset[5]}}, {B_Offset, 1'b0}};  // Bit_Extender bit_extender_1
  assign J_Offset16 = {{6{J_Offset[8]}}, {J_Offset, 1'b0}};  // Bit_Extender bit_extender_2
  assign Imm_16 = {{10{I_Imm[5]}}, I_Imm};  // Bit_Extender bit_extender_3
  assign S_Offset16 = {{10{S_Offset[5]}}, S_Offset};  // Bit_Extender bit_extender_4
  // Probe on B_Offset16
  Multiplexer #(.select(3), .width(16)) multiplexer_1 (
    .in0(Imm_16), .in1(S_Offset16), .in2(B_Offset16), .in3(J_Offset16), .out(Offset_Imm), .sel(OffSel));  // open: in4, in5, in6, in7

  // Other names for the same wires on the sheet: OffsetSel[15:0] = Offset_Imm

  // Notes on the sheet:
  //   Instrucao tipo I
  //   Offset tipo S
  //   Offset tipo B
  //   Offset tipo J
endmodule

module UC (
  input  [3:0] opcode,
  input  [2:0] funct,
  input  CLK,
  output RegWrite,
  output ALUSrc,
  output Branch,
  output MemWrite,
  output Jump,
  output MemRead,
  output MemToRead,
  output [2:0] ALUOp,
  output [2:0] OffSel
);

  wire add, addf, and_f, and_logic, Beq, Bne, I_AR, is_I, or_f, or_logic, R_Type, slt_f, sub, subf;

  Decoder #(.select(4)) decoder_1 (
    .out0(R_Type), .out1(I_AR), .out2(MemRead), .out3(MemWrite), .out4(Beq), .out5(Bne), .out6(Jump),
    .sel(opcode), .en(1'b1));  // open: out7, out8, out9, out10, out11, out12, out13, out14, out15
  Decoder #(.select(3)) decoder_2 (
    .out0(addf), .out1(subf), .out2(and_f), .out3(or_f), .out4(slt_f), .sel(funct), .en(1'b1));  // open: out5, out6, out7
  and and_1 (add, R_Type, addf);
  and and_2 (sub, R_Type, subf);
  and and_3 (and_logic, R_Type, and_f);
  and and_4 (or_logic, R_Type, or_f);
  or or_1 (is_I, I_AR, MemRead);
  or or_2 (RegWrite, is_I, Jump, R_Type);
  and and_5 (ALUOp[2], R_Type, slt_f);
  or or_3 (ALUSrc, I_AR, MemRead, MemWrite);
  or or_4 (ALUOp[0], sub, Branch);
  or or_5 (ALUOp[1], and_logic, or_logic);
  or or_6 (Branch, Beq, Bne);

  assign MemToRead = MemRead;
  assign OffSel = {Jump, Branch, MemWrite};

  // Other names for the same wires on the sheet: slt_logic = ALUOp[2]; I_Load = MemRead; SW = MemWrite; Jal = Jump

  // Notes on the sheet:
  //   OffSel
  //   ALUOp
  //   RegWrite
  //   ALUSrc
  //   Branch
endmodule

module DM (
  input  [15:0] Address,
  input  WriteEnable,
  input  MemRead,
  input  CLK,
  input  [15:0] WriteData,
  output [15:0] OutDM
);

  RAM #(.addrWidth(5), .dataWidth(16)) ram_1 (
    .addr({5{1'b0}}), .we(1'b0), .oe(1'b1), .clk(CLK), .din(WriteData), .dout(OutDM));
  // Probe on WriteData

  // Other names for the same wires on the sheet: MemWrite = WriteEnable; WD[15:0] = WriteData
endmodule

module DM2 (
  input  [4:0] Address,
  input  MemWrite,
  input  MemRead,
  input  CLK,
  input  [15:0] WiteData,
  output [15:0] DataOut
);

  wire [15:0] ram_1_dout;

  RAM #(.addrWidth(5), .dataWidth(16), .enables("line")) ram_1 (.dout(ram_1_dout));  // open: addr, we, clk, din

  // Other names for the same wires on the sheet: WD[15:0] = WiteData
endmodule
